# Fritzing sketch lock (saved by Fritzing 0.9.9b)
breadboards: 1

parts:
  Part1 = RFID-RC522-v2
  Part2 = Arduino Nano (Rev3.0)
  S1 = Toggle Switch spst [package=THT]
  BAT1 = BC9VPC [package=bc9vpc]
  Mod1 = KY-019 5V Relay Module [package="Breakout board"]
  J1 = Piezo Speaker
  VCC1 = 4 x AAA Battery Mount
  L1 = Solenoid
  C1 = Capacitor Polarized [package=cpol-radial-100uf-25v]
  U1 = WS2812 RGB LED strip

nets:
  N1: Part1.SDA, Part2.D9
  N2: Part1.SCK, Part2.D12/MISO
  N3: Part1.MOSI, Part2.D11/MOSI
  N4: Part1.MISO, Part2.D10
  GND: Part1.GND, Part2.GND, BAT1.V-, Mod1.-, J1.pin1, C1.-, U1.GND
  N5: Part1.RST, Part2.D8
  3.3V: Part1.3.3V, Part2.VIN, S1.COM, Mod1.+, C1.+, U1.VCC
  N6: Part2.D2, J1.pin2
  N7: Part2.D3, Mod1.S
  N8: Part2.D5, U1.DIN
  N9: S1.L1, BAT1.V+
  N10: Mod1.Common, L1.pin2
  N11: Mod1.NO, VCC1.+
  N12: VCC1.-, L1.pin1

custom parts:
  RFID-RC522-v2: A simple China made RFID-RC522 Reader; do check the pin labels, as this is a MFRC522 based clone.
  Toggle Switch spst: Toggle Switch single pole single throw
  KY-019 5V Relay Module: KY-019 5V Relay module, used to control AC circuits. (Special thanks to vanepp for fixing the PCB holes and other errors)
  WS2812 RGB LED strip: WS2812 strip
